// Logisim project μMIPStmp.circ as structural Verilog
module Register_File (
  input  [15:0] Write_Data,
  input  [15:0] Write_Data_2,
  input  Write_Enable,
  input  Overflow,
  input  [2:0] Write__r,
  input  [2:0] Read__r1,
  input  [2:0] Read__r2,
  output [15:0] Read__r1_2,
  output [15:0] Read__r2_2
);

  wire clock_1_out, or_1_out, or_2_out, or_3_out, or_4_out, or_5_out, or_6_out, or_7_out, or_8_out, r0, r0_2,
       r1, r1_2, r2, r2_2, r3, r3_2, r4, r4_2, r5, r5_2, r6, r6_2, r7, r7_2;
  wire [2:0] adder_1_out;
  wire [15:0] multiplexer_1_out, multiplexer_2_out, multiplexer_3_out, multiplexer_4_out, multiplexer_5_out,
       multiplexer_6_out, multiplexer_7_out, multiplexer_8_out, r0_q, r1_q, r2_q, r3_q, r4_q, r5_q, r6_q,
       r7_q;

  Clock clock_1 (.out(clock_1_out));
  Adder #(.width(3)) adder_1 (.a(Write__r), .b(3'b001), .out(adder_1_out));  // open: cin, cout
  Demultiplexer #(.select(3)) demultiplexer_1 (
    .out0(r0), .out1(r1), .out2(r2), .out3(r3), .out4(r4), .out5(r5), .out6(r6), .out7(r7),
    .in(Write_Enable), .sel(Write__r));  // open: en
  Demultiplexer #(.select(3)) demultiplexer_2 (
    .out0(r0_2), .out1(r1_2), .out2(r2_2), .out3(r3_2), .out4(r4_2), .out5(r5_2), .out6(r6_2), .out7(r7_2),
    .in(Overflow), .sel(adder_1_out));  // open: en
  Multiplexer #(.width(16)) multiplexer_1 (
    .in0(Write_Data), .in1(Write_Data_2), .out(multiplexer_1_out), .sel(r0_2));  // open: en
  Multiplexer #(.width(16)) multiplexer_2 (
    .in0(Write_Data), .in1(Write_Data_2), .out(multiplexer_2_out), .sel(r1_2));  // open: en
  Multiplexer #(.width(16)) multiplexer_3 (
    .in0(Write_Data), .in1(Write_Data_2), .out(multiplexer_3_out), .sel(r2_2));  // open: en
  Multiplexer #(.width(16)) multiplexer_4 (
    .in0(Write_Data), .in1(Write_Data_2), .out(multiplexer_4_out), .sel(r3_2));  // open: en
  Multiplexer #(.width(16)) multiplexer_5 (
    .in0(Write_Data), .in1(Write_Data_2), .out(multiplexer_5_out), .sel(r4_2));  // open: en
  Multiplexer #(.width(16)) multiplexer_6 (
    .in0(Write_Data), .in1(Write_Data_2), .out(multiplexer_6_out), .sel(r5_2));  // open: en
  Multiplexer #(.width(16)) multiplexer_7 (
    .in0(Write_Data), .in1(Write_Data_2), .out(multiplexer_7_out), .sel(r6_2));  // open: en
  Multiplexer #(.width(16)) multiplexer_8 (
    .in0(Write_Data), .in1(Write_Data_2), .out(multiplexer_8_out), .sel(r7_2));  // open: en
  or or_1 (or_1_out, r0, r0_2);
  or or_2 (or_2_out, r1, r1_2);
  or or_3 (or_3_out, r2, r2_2);
  or or_4 (or_4_out, r3, r3_2);
  or or_5 (or_5_out, r4, r4_2);
  or or_6 (or_6_out, r5, r5_2);
  or or_7 (or_7_out, r6, r6_2);
  or or_8 (or_8_out, r7, r7_2);
  Register #(.width(16)) u_r0 (.D(multiplexer_1_out), .en(or_1_out), .Q(r0_q), .clk(clock_1_out));  // open: clr
  Register #(.width(16)) u_r1 (.D(multiplexer_2_out), .en(or_2_out), .Q(r1_q), .clk(clock_1_out));  // open: clr
  Register #(.width(16)) u_r2 (.D(multiplexer_3_out), .en(or_3_out), .Q(r2_q), .clk(clock_1_out));  // open: clr
  Register #(.width(16)) u_r3 (.D(multiplexer_4_out), .en(or_4_out), .Q(r3_q), .clk(clock_1_out));  // open: clr
  Register #(.width(16)) u_r4 (.D(multiplexer_5_out), .en(or_5_out), .Q(r4_q), .clk(clock_1_out));  // open: clr
  Register #(.width(16)) u_r5 (.D(multiplexer_6_out), .en(or_6_out), .Q(r5_q), .clk(clock_1_out));  // open: clr
  Register #(.width(16)) u_r6 (.D(multiplexer_7_out), .en(or_7_out), .Q(r6_q), .clk(clock_1_out));  // open: clr
  Register #(.width(16)) u_r7 (.D(multiplexer_8_out), .en(or_8_out), .Q(r7_q), .clk(clock_1_out));  // open: clr
  Multiplexer #(.select(3), .width(16)) multiplexer_9 (
    .in0(r0_q), .in1(r1_q), .in2(r2_q), .in3(r3_q), .in4(r4_q), .in5(r5_q), .in6(r6_q), .in7(r7_q),
    .out(Read__r1_2), .sel(Read__r1));  // open: en
  Multiplexer #(.select(3), .width(16)) multiplexer_10 (
    .in0(r0_q), .in1(r1_q), .in2(r2_q), .in3(r3_q), .in4(r4_q), .in5(r5_q), .in6(r6_q), .in7(r7_q),
    .out(Read__r2_2), .sel(Read__r2));  // open: en

  // Other names for the same wires on the sheet: Data_1[15:0] = Write_Data; Data_2[15:0] = Write_Data_2

  // Notes on the sheet:
  //   Clock
endmodule
